// Logisim project week1.circ as structural Verilog: 1 circuit, main circuit main
module main (
);

  wire and_1_out, and_2_out, and_3_out, or_1_out, undriven, undriven_2, undriven_3, undriven_4, undriven_5,
       xor_1_out, xor_2_out, xor_3_out;

  xor xor_1 (xor_1_out, undriven, undriven_2);
  and and_1 (and_1_out, undriven_2, undriven);
  xor xor_2 (xor_2_out, undriven_3, undriven_4);
  xor xor_3 (xor_3_out, xor_2_out, undriven_5);
  and and_2 (and_2_out, xor_2_out, undriven_5);
  and and_3 (and_3_out, undriven_3, undriven_4);
  or or_1 (or_1_out, and_2_out, and_3_out);

  // Notes on the sheet:
  //   x
  //   y
  //   binary half adder
  //   sum
  //   carry bit
  //   x
  //   y
  //   z
  //   binary full adder
  //   sum1
  //   sum2
endmodule
