// Logisim project week2.circ as structural Verilog: 3 circuits, main circuit main
module main (
  input  in_1,
  input  in_2,
  input  in_3,
  input  in_4,
  input  in_5,
  input  in_6,
  input  in_7,
  input  in_8,
  input  in_9,
  input  in_10,
  input  in_11,
  input  in_12,
  input  in_13,
  input  in_14,
  input  in_15,
  input  in_16
);

  wire and_1_out, and_2_out, and_3_out, and_4_out, and_5_out, and_6_out, and_7_out, fulladder_1_out0,
       fulladder_1_out1, fulladder_2_out0, fulladder_2_out1, fulladder_3_out0, fulladder_3_out1,
       halfadder_1_carry, halfadder_1_out0, or_1_out, or_2_out, or_3_out, xor_1_out, xor_2_out, xor_3_out,
       xor_4_out, xor_5_out, xor_6_out, xor_7_out;

  xor xor_1 (xor_1_out, in_1, in_4);
  and and_1 (and_1_out, in_1, in_4);
  xor xor_2 (xor_2_out, in_8, in_10);
  and and_2 (and_2_out, in_8, in_10);
  xor xor_3 (xor_3_out, in_13, in_14);
  and and_3 (and_3_out, in_13, in_14);
  xor xor_4 (xor_4_out, in_15, in_16);
  and and_4 (and_4_out, in_15, in_16);
  xor xor_5 (xor_5_out, and_1_out, xor_2_out);
  and and_5 (and_5_out, and_1_out, xor_2_out);
  xor xor_6 (xor_6_out, or_1_out, xor_3_out);
  and and_6 (and_6_out, or_1_out, xor_3_out);
  xor xor_7 (xor_7_out, or_2_out, xor_4_out);
  and and_7 (and_7_out, or_2_out, xor_4_out);
  or or_1 (or_1_out, and_5_out, and_2_out);
  or or_2 (or_2_out, and_6_out, and_3_out);
  or or_3 (or_3_out, and_7_out, and_4_out);
  LED led_1 (.in(xor_1_out));
  LED led_2 (.in(xor_5_out));
  LED led_3 (.in(xor_6_out));
  LED led_4 (.in(xor_7_out));
  LED led_5 (.in(or_3_out));
  halfadder halfadder_1 (.IN0(in_2), .IN1(in_3), .OUT0(halfadder_1_out0), .CARRY(halfadder_1_carry));
  LED led_6 (.in(halfadder_1_out0));
  fulladder fulladder_1 (
    .CARRYIN(halfadder_1_carry), .IN0(in_5), .IN1(in_6), .OUT0(fulladder_1_out0), .OUT1(fulladder_1_out1));
  LED led_7 (.in(fulladder_1_out0));
  fulladder fulladder_2 (
    .CARRYIN(fulladder_1_out1), .IN0(in_7), .IN1(in_9), .OUT0(fulladder_2_out0), .OUT1(fulladder_2_out1));
  LED led_8 (.in(fulladder_2_out0));
  fulladder fulladder_3 (
    .CARRYIN(fulladder_2_out1), .IN0(in_11), .IN1(in_12), .OUT0(fulladder_3_out0), .OUT1(fulladder_3_out1));
  LED led_9 (.in(fulladder_3_out0));
  LED led_10 (.in(fulladder_3_out1));

  // Notes on the sheet:
  //   4 bit Binary Adder
  //   starts off with a half adder
  //   carry bit linked to carry input of next full adder
  //   overflow/carry bit
endmodule

module halfadder (
  input  IN0,
  input  IN1,
  output OUT0,
  output CARRY
);

  xor xor_1 (OUT0, IN0, IN1);
  and and_1 (CARRY, IN0, IN1);
endmodule

module fulladder (
  input  CARRYIN,
  input  IN0,
  input  IN1,
  output OUT0,
  output OUT1
);

  wire halfadder_1_carry, halfadder_1_out0, halfadder_2_carry;

  halfadder halfadder_1 (.IN0(IN0), .IN1(IN1), .OUT0(halfadder_1_out0), .CARRY(halfadder_1_carry));
  halfadder halfadder_2 (.IN0(CARRYIN), .IN1(halfadder_1_out0), .OUT0(OUT0), .CARRY(halfadder_2_carry));
  or or_1 (OUT1, halfadder_2_carry, halfadder_1_carry);
endmodule
