// Logisim project assign1.circ as structural Verilog: 7 circuits, main circuit main
module main (
);

  wire clock_1_out, NextTrack_out, not_1_out, not_2_out, not_3_out, not_4_out, OnOff_out, or_1_out,
       Pause_out, Play_out, PreviousTrack_out, stagefour_1_power, stageone_1_paused, stageone_1_playing,
       stagetwo_1_vol0, stagetwo_1_vol1, stagetwo_1_vol2, stagetwo_1_vol3, stagetwo_1_vol4, stagetwo_1_vol5,
       stagetwo_1_vol6, stagetwo_1_vol7, VolumeDown_out, VolumeUp_out;
  wire [3:0] bonus_1_min0, bonus_1_min4, bonus_1_sec0, bonus_1_sec4, stagethree_1_ones0, stagethree_1_tens0;

  Clock clock_1 (.out(clock_1_out));
  Button OnOff (.out(OnOff_out));
  Button Pause (.out(Pause_out));
  Button Play (.out(Play_out));
  Button VolumeDown (.out(VolumeDown_out));
  Button VolumeUp (.out(VolumeUp_out));
  Button PreviousTrack (.out(PreviousTrack_out));
  Button NextTrack (.out(NextTrack_out));
  not not_1 (not_1_out, stagefour_1_power);
  not not_2 (not_2_out, stagefour_1_power);
  not not_3 (not_3_out, stagefour_1_power);
  or or_1 (or_1_out, PreviousTrack_out, NextTrack_out);
  not not_4 (not_4_out, stagefour_1_power);
  LED Power (.in(stagefour_1_power));
  StageOne stageone_1 (
    .Play(Play_out), .Pause(Pause_out), .CLK(clock_1_out), .CircOn(stagefour_1_power), .CircOff(not_1_out),
    .Playing(stageone_1_playing), .Paused(stageone_1_paused));
  LED Playing (.in(stageone_1_playing));
  LED Paused (.in(stageone_1_paused));
  StageTwo stagetwo_1 (
    .VolUp(VolumeUp_out), .VolDown(VolumeDown_out), .CLK(clock_1_out), .CircOn(stagefour_1_power),
    .CircOff(not_2_out), .vol0(stagetwo_1_vol0), .vol1(stagetwo_1_vol1), .vol2(stagetwo_1_vol2),
    .vol3(stagetwo_1_vol3), .vol4(stagetwo_1_vol4), .vol5(stagetwo_1_vol5), .vol6(stagetwo_1_vol6),
    .vol7(stagetwo_1_vol7));
  StageThree stagethree_1 (
    .NextTrack(NextTrack_out), .PreviousTrack(PreviousTrack_out), .CLK(clock_1_out),
    .CircOn(stagefour_1_power), .CircOff(not_3_out), .ones0(stagethree_1_ones0[0]),
    .ones1(stagethree_1_ones0[1]), .ones2(stagethree_1_ones0[2]), .ones3(stagethree_1_ones0[3]),
    .tens0(stagethree_1_tens0[0]), .tens1(stagethree_1_tens0[1]), .tens2(stagethree_1_tens0[2]),
    .tens3(stagethree_1_tens0[3]));
  StageFour stagefour_1 (.Switch(OnOff_out), .CLK(clock_1_out), .Power(stagefour_1_power));
  Bonus bonus_1 (
    .Reset(or_1_out), .Playing(stageone_1_playing), .CLK(clock_1_out), .CircOn(stagefour_1_power),
    .CircOff(not_4_out), .sec0(bonus_1_sec0[0]), .sec1(bonus_1_sec0[1]), .sec2(bonus_1_sec0[2]),
    .sec3(bonus_1_sec0[3]), .sec4(bonus_1_sec4[0]), .sec5(bonus_1_sec4[1]), .sec6(bonus_1_sec4[2]),
    .sec7(bonus_1_sec4[3]), .min0(bonus_1_min0[0]), .min1(bonus_1_min0[1]), .min2(bonus_1_min0[2]),
    .min3(bonus_1_min0[3]), .min4(bonus_1_min4[0]), .min5(bonus_1_min4[1]), .min6(bonus_1_min4[2]),
    .min7(bonus_1_min4[3]));
  LED led_1 (.in(stagetwo_1_vol0));
  LED led_2 (.in(stagetwo_1_vol1));
  LED led_3 (.in(stagetwo_1_vol2));
  LED led_4 (.in(stagetwo_1_vol3));
  Hex_Digit_Display hex_digit_display_1 (.value(bonus_1_min4));  // open: dp
  LED led_5 (.in(stagetwo_1_vol4));
  LED led_6 (.in(stagetwo_1_vol5));
  LED led_7 (.in(stagetwo_1_vol6));
  LED led_8 (.in(stagetwo_1_vol7));
  Hex_Digit_Display hex_digit_display_2 (.value(bonus_1_min0));  // open: dp
  Hex_Digit_Display hex_digit_display_3 (.value(bonus_1_sec4));  // open: dp
  Hex_Digit_Display hex_digit_display_4 (.value(stagethree_1_tens0));  // open: dp
  Hex_Digit_Display hex_digit_display_5 (.value(bonus_1_sec0));  // open: dp
  Hex_Digit_Display hex_digit_display_6 (.value(stagethree_1_ones0));  // open: dp

  // Notes on the sheet:
  //   Volume
  //   Minutes
  //   Seconds
  //   TrackNumber
endmodule

module StageOne (
  input  Play,
  input  Pause,
  input  CLK,
  input  CircOn,
  input  CircOff,
  output Playing,
  output Paused
);

  wire d_ff_1_q, d_ff_2_q, j_k_ff_1_q, j_k_ff_1_qn, j_k_ff_2_q, j_k_ff_2_qn, or_1_out;

  J_K_Flip_Flop j_k_ff_1 (.J(CircOn), .K(CircOff), .clk(CLK), .Q(j_k_ff_1_q), .Qn(j_k_ff_1_qn));  // open: preset, reset
  D_Flip_Flop d_ff_1 (.D(Play), .clk(CLK), .Q(d_ff_1_q), .preset(Play));  // open: Qn, reset
  D_Flip_Flop d_ff_2 (.D(Pause), .clk(CLK), .Q(d_ff_2_q), .preset(Pause));  // open: Qn, reset
  J_K_Flip_Flop j_k_ff_2 (
    .J(or_1_out), .K(d_ff_2_q), .clk(CLK), .Q(j_k_ff_2_q), .Qn(j_k_ff_2_qn), .reset(j_k_ff_1_qn));  // open: preset
  or or_1 (or_1_out, d_ff_1_q, d_ff_2_q);
  and and_1 (Playing, j_k_ff_1_q, j_k_ff_2_q);
  and and_2 (Paused, j_k_ff_2_qn, j_k_ff_1_q);
endmodule

module StageTwo (
  input  VolUp,
  input  VolDown,
  input  CLK,
  input  CircOn,
  input  CircOff,
  output vol0,
  output vol1,
  output vol2,
  output vol3,
  output vol4,
  output vol5,
  output vol6,
  output vol7
);

  wire and_1_out, and_2_out, and_3_out, and_4_out, and_5_out, and_7_out, and_9_out, and_11_out, and_12_out,
       and_13_out, and_14_out, and_16_out, and_18_out, and_19_out, and_20_out, and_22_out, and_24_out,
       d_ff_1_q, d_ff_2_q, d_ff_3_q, d_ff_4_q, d_ff_5_q, d_ff_6_q, d_ff_7_q, d_ff_8_q, j_k_ff_1_q, not_1_out,
       or_1_out, or_2_out, or_3_out, or_4_out, or_5_out, or_6_out, or_7_out, or_8_out, or_9_out;

  J_K_Flip_Flop j_k_ff_1 (.J(CircOn), .K(CircOff), .clk(CLK), .Q(j_k_ff_1_q));  // open: Qn, preset, reset
  not not_1 (not_1_out, VolUp);
  and and_1 (and_1_out, VolUp, VolUp);
  or or_1 (or_1_out, VolDown, VolUp);
  and and_2 (and_2_out, or_1_out, CLK, j_k_ff_1_q);
  and and_3 (and_3_out, not_1_out, d_ff_2_q);
  or or_2 (or_2_out, and_1_out, and_3_out);
  D_Flip_Flop d_ff_1 (.D(or_2_out), .clk(and_2_out), .Q(d_ff_1_q));  // open: Qn, preset, reset
  and and_4 (and_4_out, not_1_out, d_ff_3_q);
  and and_5 (and_5_out, d_ff_1_q, VolUp);
  or or_3 (or_3_out, and_5_out, and_4_out);
  D_Flip_Flop d_ff_2 (.D(or_3_out), .clk(and_2_out), .Q(d_ff_2_q));  // open: Qn, preset, reset
  and and_6 (vol0, d_ff_1_q, j_k_ff_1_q);
  and and_7 (and_7_out, d_ff_2_q, VolUp);
  or or_4 (or_4_out, and_7_out, and_9_out);
  and and_8 (vol1, d_ff_2_q, j_k_ff_1_q);
  and and_9 (and_9_out, not_1_out, d_ff_4_q);
  D_Flip_Flop d_ff_3 (.D(or_4_out), .clk(and_2_out), .Q(d_ff_3_q));  // open: Qn, preset, reset
  and and_10 (vol2, d_ff_3_q, j_k_ff_1_q);
  and and_11 (and_11_out, not_1_out, d_ff_5_q);
  and and_12 (and_12_out, d_ff_3_q, VolUp);
  or or_5 (or_5_out, and_12_out, and_11_out);
  D_Flip_Flop d_ff_4 (.D(or_5_out), .clk(and_2_out), .Q(d_ff_4_q));  // open: Qn, preset, reset
  and and_13 (and_13_out, not_1_out, d_ff_6_q);
  and and_14 (and_14_out, d_ff_4_q, VolUp);
  or or_6 (or_6_out, and_14_out, and_13_out);
  D_Flip_Flop d_ff_5 (.D(or_6_out), .clk(and_2_out), .Q(d_ff_5_q));  // open: Qn, preset, reset
  and and_15 (vol3, d_ff_4_q, j_k_ff_1_q);
  and and_16 (and_16_out, d_ff_5_q, VolUp);
  and and_17 (vol4, d_ff_5_q, j_k_ff_1_q);
  and and_18 (and_18_out, not_1_out, d_ff_7_q);
  or or_7 (or_7_out, and_16_out, and_18_out);
  D_Flip_Flop d_ff_6 (.D(or_7_out), .clk(and_2_out), .Q(d_ff_6_q));  // open: Qn, preset, reset
  and and_19 (and_19_out, d_ff_6_q, VolUp);
  and and_20 (and_20_out, not_1_out, d_ff_8_q);
  or or_8 (or_8_out, and_19_out, and_20_out);
  D_Flip_Flop d_ff_7 (.D(or_8_out), .clk(and_2_out), .Q(d_ff_7_q));  // open: Qn, preset, reset
  and and_21 (vol5, d_ff_6_q, j_k_ff_1_q);
  and and_22 (and_22_out, d_ff_7_q, VolUp);
  or or_9 (or_9_out, and_22_out, and_24_out);
  D_Flip_Flop d_ff_8 (.D(or_9_out), .clk(and_2_out), .Q(d_ff_8_q));  // open: Qn, preset, reset
  and and_23 (vol6, d_ff_7_q, j_k_ff_1_q);
  and and_24 (and_24_out, not_1_out, 1'b0);
  and and_25 (vol7, d_ff_8_q, j_k_ff_1_q);
endmodule

module StageThree (
  input  NextTrack,
  input  PreviousTrack,
  input  CLK,
  input  CircOn,
  input  CircOff,
  output ones0,
  output ones1,
  output ones2,
  output ones3,
  output tens0,
  output tens1,
  output tens2,
  output tens3
);

  wire and_1_out, and_2_out, and_3_out, and_4_out, and_5_out, and_6_out, and_7_out, and_8_out, and_9_out,
       and_10_out, and_11_out, and_12_out, and_13_out, and_14_out, and_15_out, and_16_out, and_17_out,
       j_k_ff_1_q, j_k_ff_1_qn, or_1_out, or_2_out, or_3_out, or_4_out, or_5_out, or_6_out, or_7_out,
       or_8_out, or_9_out, or_10_out, or_11_out, or_12_out, or_13_out, t_ff_1_q, t_ff_1_qn, t_ff_2_q,
       t_ff_2_qn, t_ff_3_q, t_ff_3_qn, t_ff_4_q, t_ff_4_qn, t_ff_5_q, t_ff_5_qn, t_ff_6_q, t_ff_6_qn,
       t_ff_7_q, t_ff_8_q;

  J_K_Flip_Flop j_k_ff_1 (.J(CircOn), .K(CircOff), .clk(CLK), .Q(j_k_ff_1_q), .Qn(j_k_ff_1_qn));  // open: preset, reset
  and and_1 (and_1_out, CLK, j_k_ff_1_q);
  or or_1 (or_1_out, and_10_out, and_16_out);
  T_Flip_Flop t_ff_1 (.T(or_2_out), .clk(and_1_out), .Q(t_ff_1_q), .Qn(t_ff_1_qn), .reset(and_16_out));  // open: preset
  or or_2 (or_2_out, NextTrack, PreviousTrack);
  T_Flip_Flop t_ff_2 (.T(or_3_out), .clk(or_1_out), .Q(t_ff_2_q), .Qn(t_ff_2_qn), .reset(and_17_out));  // open: preset
  or or_3 (or_3_out, NextTrack, PreviousTrack);
  and and_2 (and_2_out, NextTrack, t_ff_1_q);
  or or_4 (or_4_out, and_2_out, and_3_out);
  and and_3 (and_3_out, t_ff_1_qn, PreviousTrack);
  and and_4 (and_4_out, NextTrack, t_ff_2_q);
  or or_5 (or_5_out, and_4_out, and_5_out);
  and and_5 (and_5_out, t_ff_2_qn, PreviousTrack);
  T_Flip_Flop t_ff_3 (.T(or_4_out), .clk(and_1_out), .Q(t_ff_3_q), .Qn(t_ff_3_qn), .reset(or_6_out));  // open: preset
  or or_6 (or_6_out, and_16_out, and_10_out);
  T_Flip_Flop t_ff_4 (.T(or_5_out), .clk(or_1_out), .Q(t_ff_4_q), .Qn(t_ff_4_qn), .reset(or_7_out));  // open: preset
  or or_7 (or_7_out, and_17_out, and_13_out);
  and and_6 (and_6_out, and_2_out, t_ff_3_q);
  and and_7 (and_7_out, t_ff_3_qn, and_3_out);
  and and_8 (and_8_out, and_4_out, t_ff_4_q);
  and and_9 (and_9_out, t_ff_4_qn, and_5_out);
  T_Flip_Flop t_ff_5 (.T(or_8_out), .clk(and_1_out), .Q(t_ff_5_q), .Qn(t_ff_5_qn), .reset(or_9_out));  // open: preset
  or or_8 (or_8_out, and_6_out, and_7_out);
  or or_9 (or_9_out, and_16_out, and_10_out);
  T_Flip_Flop t_ff_6 (.T(or_10_out), .clk(or_1_out), .Q(t_ff_6_q), .Qn(t_ff_6_qn), .reset(or_11_out));  // open: preset
  or or_10 (or_10_out, and_8_out, and_9_out);
  or or_11 (or_11_out, and_17_out, and_13_out);
  and and_10 (and_10_out, PreviousTrack, t_ff_1_q, t_ff_3_q, t_ff_5_q, t_ff_7_q);
  and and_11 (and_11_out, and_6_out, t_ff_5_q);
  and and_12 (and_12_out, t_ff_5_qn, and_7_out);
  and and_13 (and_13_out, PreviousTrack, t_ff_2_q, t_ff_4_q, t_ff_6_q, t_ff_8_q);
  and and_14 (and_14_out, and_8_out, t_ff_6_q);
  and and_15 (and_15_out, t_ff_6_qn, and_9_out);
  T_Flip_Flop t_ff_7 (.T(or_12_out), .clk(and_1_out), .Q(t_ff_7_q), .reset(and_16_out));  // open: Qn, preset
  or or_12 (or_12_out, and_11_out, and_12_out);
  T_Flip_Flop t_ff_8 (.T(or_13_out), .clk(or_1_out), .Q(t_ff_8_q), .reset(and_17_out));  // open: Qn, preset
  or or_13 (or_13_out, and_14_out, and_15_out);
  and and_16 (and_16_out, NextTrack, t_ff_3_q, t_ff_7_q);
  and and_17 (and_17_out, NextTrack, t_ff_4_q, t_ff_8_q);
  D_Flip_Flop d_ff_1 (.D(t_ff_1_q), .clk(and_1_out), .Q(ones0), .reset(j_k_ff_1_qn));  // open: Qn, preset
  D_Flip_Flop d_ff_2 (.D(t_ff_2_q), .clk(and_1_out), .Q(tens0), .reset(j_k_ff_1_qn));  // open: Qn, preset
  D_Flip_Flop d_ff_3 (.D(t_ff_5_q), .clk(and_1_out), .Q(ones2), .reset(j_k_ff_1_qn));  // open: Qn, preset
  D_Flip_Flop d_ff_4 (.D(t_ff_3_q), .clk(and_1_out), .Q(ones1), .reset(j_k_ff_1_qn));  // open: Qn, preset
  D_Flip_Flop d_ff_5 (.D(t_ff_4_q), .clk(and_1_out), .Q(tens1), .reset(j_k_ff_1_qn));  // open: Qn, preset
  D_Flip_Flop d_ff_6 (.D(t_ff_7_q), .clk(and_1_out), .Q(ones3), .reset(j_k_ff_1_qn));  // open: Qn, preset
  D_Flip_Flop d_ff_7 (.D(t_ff_6_q), .clk(and_1_out), .Q(tens2), .reset(j_k_ff_1_qn));  // open: Qn, preset
  D_Flip_Flop d_ff_8 (.D(t_ff_8_q), .clk(and_1_out), .Q(tens3), .reset(j_k_ff_1_qn));  // open: Qn, preset
  Hex_Digit_Display hex_digit_display_1 (.value({tens3, tens2, tens1, tens0}));  // open: dp
  Hex_Digit_Display hex_digit_display_2 (.value({ones3, ones2, ones1, ones0}));  // open: dp
endmodule

module StageFour (
  input  Switch,
  input  CLK,
  output Power
);

  wire d_ff_1_q;

  D_Flip_Flop d_ff_1 (.D(Switch), .clk(CLK), .Q(d_ff_1_q), .preset(Switch));  // open: Qn, reset
  J_K_Flip_Flop j_k_ff_1 (.J(d_ff_1_q), .K(d_ff_1_q), .clk(CLK), .Q(Power));  // open: Qn, preset, reset
endmodule

module Bonus (
  input  Reset,
  input  Playing,
  input  CLK,
  input  CircOn,
  input  CircOff,
  output sec0,
  output sec1,
  output sec2,
  output sec3,
  output sec4,
  output sec5,
  output sec6,
  output sec7,
  output min0,
  output min1,
  output min2,
  output min3,
  output min4,
  output min5,
  output min6,
  output min7
);

  wire and_1_out, and_2_out, and_3_out, and_4_out, and_5_out, and_6_out, and_7_out, and_8_out, and_9_out,
       and_10_out, and_11_out, and_12_out, and_13_out, and_14_out, and_15_out, and_16_out, and_17_out,
       j_k_ff_1_q, j_k_ff_1_qn, or_1_out, or_2_out, or_3_out, or_4_out, t_ff_1_q, t_ff_2_q, t_ff_3_q,
       t_ff_4_q, t_ff_5_q, t_ff_6_q, t_ff_7_q, t_ff_8_q, t_ff_9_q, t_ff_10_q, t_ff_11_q, t_ff_12_q,
       t_ff_13_q, t_ff_14_q, t_ff_15_q, t_ff_16_q;

  J_K_Flip_Flop j_k_ff_1 (.J(CircOn), .K(CircOff), .clk(CLK), .Q(j_k_ff_1_q), .Qn(j_k_ff_1_qn));  // open: preset, reset
  and and_1 (and_1_out, CLK, j_k_ff_1_q);
  T_Flip_Flop t_ff_1 (.T(Playing), .clk(and_1_out), .Q(t_ff_1_q), .reset(or_1_out));  // open: Qn, preset
  T_Flip_Flop t_ff_2 (.T(Playing), .clk(and_14_out), .Q(t_ff_2_q), .reset(or_2_out));  // open: Qn, preset
  T_Flip_Flop t_ff_3 (.T(Playing), .clk(and_15_out), .Q(t_ff_3_q), .reset(or_3_out));  // open: Qn, preset
  T_Flip_Flop t_ff_4 (.T(Playing), .clk(and_16_out), .Q(t_ff_4_q), .reset(or_4_out));  // open: Qn, preset
  T_Flip_Flop t_ff_5 (.T(and_2_out), .clk(and_1_out), .Q(t_ff_5_q), .reset(or_1_out));  // open: Qn, preset
  and and_2 (and_2_out, Playing, t_ff_1_q);
  and and_3 (and_3_out, Playing, t_ff_2_q);
  T_Flip_Flop t_ff_6 (.T(and_3_out), .clk(and_14_out), .Q(t_ff_6_q), .reset(or_2_out));  // open: Qn, preset
  and and_4 (and_4_out, Playing, t_ff_3_q);
  T_Flip_Flop t_ff_7 (.T(and_4_out), .clk(and_15_out), .Q(t_ff_7_q), .reset(or_3_out));  // open: Qn, preset
  and and_5 (and_5_out, Playing, t_ff_4_q);
  T_Flip_Flop t_ff_8 (.T(and_5_out), .clk(and_16_out), .Q(t_ff_8_q), .reset(or_4_out));  // open: Qn, preset
  and and_6 (and_6_out, and_2_out, t_ff_5_q);
  and and_7 (and_7_out, and_3_out, t_ff_6_q);
  and and_8 (and_8_out, and_4_out, t_ff_7_q);
  and and_9 (and_9_out, and_5_out, t_ff_8_q);
  T_Flip_Flop t_ff_9 (.T(and_6_out), .clk(and_1_out), .Q(t_ff_9_q), .reset(or_1_out));  // open: Qn, preset
  T_Flip_Flop t_ff_10 (.T(and_7_out), .clk(and_14_out), .Q(t_ff_10_q), .reset(or_2_out));  // open: Qn, preset
  T_Flip_Flop t_ff_11 (.T(and_8_out), .clk(and_15_out), .Q(t_ff_11_q), .reset(or_3_out));  // open: Qn, preset
  T_Flip_Flop t_ff_12 (.T(and_9_out), .clk(and_16_out), .Q(t_ff_12_q), .reset(or_4_out));  // open: Qn, preset
  and and_10 (and_10_out, and_6_out, t_ff_9_q);
  T_Flip_Flop t_ff_13 (.T(and_10_out), .clk(and_1_out), .Q(t_ff_13_q), .reset(or_1_out));  // open: Qn, preset
  T_Flip_Flop t_ff_14 (.T(and_11_out), .clk(and_14_out), .Q(t_ff_14_q), .reset(or_2_out));  // open: Qn, preset
  and and_11 (and_11_out, and_7_out, t_ff_10_q);
  T_Flip_Flop t_ff_15 (.T(and_12_out), .clk(and_15_out), .Q(t_ff_15_q), .reset(or_3_out));  // open: Qn, preset
  and and_12 (and_12_out, and_8_out, t_ff_11_q);
  T_Flip_Flop t_ff_16 (.T(and_13_out), .clk(and_16_out), .Q(t_ff_16_q), .reset(or_4_out));  // open: Qn, preset
  and and_13 (and_13_out, and_9_out, t_ff_12_q);
  and and_14 (and_14_out, t_ff_5_q, t_ff_13_q);
  and and_15 (and_15_out, t_ff_10_q, t_ff_6_q);
  and and_16 (and_16_out, t_ff_7_q, t_ff_15_q);
  and and_17 (and_17_out, t_ff_12_q, t_ff_8_q);
  or or_1 (or_1_out, and_14_out, Reset, or_4_out, and_15_out);
  or or_2 (or_2_out, and_15_out, Reset);
  or or_3 (or_3_out, and_16_out, Reset, and_17_out);
  or or_4 (or_4_out, and_17_out, Reset);
  D_Flip_Flop d_ff_1 (.D(t_ff_1_q), .clk(and_1_out), .Q(sec0), .reset(j_k_ff_1_qn));  // open: Qn, preset
  D_Flip_Flop d_ff_2 (.D(t_ff_2_q), .clk(and_1_out), .Q(sec4), .reset(j_k_ff_1_qn));  // open: Qn, preset
  D_Flip_Flop d_ff_3 (.D(t_ff_3_q), .clk(and_1_out), .Q(min0), .reset(j_k_ff_1_qn));  // open: Qn, preset
  D_Flip_Flop d_ff_4 (.D(t_ff_4_q), .clk(and_1_out), .Q(min4), .reset(j_k_ff_1_qn));  // open: Qn, preset
  D_Flip_Flop d_ff_5 (.D(t_ff_5_q), .clk(and_1_out), .Q(sec1), .reset(j_k_ff_1_qn));  // open: Qn, preset
  D_Flip_Flop d_ff_6 (.D(t_ff_6_q), .clk(and_1_out), .Q(sec5), .reset(j_k_ff_1_qn));  // open: Qn, preset
  D_Flip_Flop d_ff_7 (.D(t_ff_7_q), .clk(and_1_out), .Q(min1), .reset(j_k_ff_1_qn));  // open: Qn, preset
  D_Flip_Flop d_ff_8 (.D(t_ff_8_q), .clk(and_1_out), .Q(min5), .reset(j_k_ff_1_qn));  // open: Qn, preset
  D_Flip_Flop d_ff_9 (.D(t_ff_9_q), .clk(and_1_out), .Q(sec2), .reset(j_k_ff_1_qn));  // open: Qn, preset
  D_Flip_Flop d_ff_10 (.D(t_ff_10_q), .clk(and_1_out), .Q(sec6), .reset(j_k_ff_1_qn));  // open: Qn, preset
  D_Flip_Flop d_ff_11 (.D(t_ff_11_q), .clk(and_1_out), .Q(min2), .reset(j_k_ff_1_qn));  // open: Qn, preset
  D_Flip_Flop d_ff_12 (.D(t_ff_12_q), .clk(and_1_out), .Q(min6), .reset(j_k_ff_1_qn));  // open: Qn, preset
  D_Flip_Flop d_ff_13 (.D(t_ff_13_q), .clk(and_1_out), .Q(sec3), .reset(j_k_ff_1_qn));  // open: Qn, preset
  D_Flip_Flop d_ff_14 (.D(t_ff_14_q), .clk(and_1_out), .Q(sec7), .reset(j_k_ff_1_qn));  // open: Qn, preset
  D_Flip_Flop d_ff_15 (.D(t_ff_15_q), .clk(and_1_out), .Q(min3), .reset(j_k_ff_1_qn));  // open: Qn, preset
  D_Flip_Flop d_ff_16 (.D(t_ff_16_q), .clk(and_1_out), .Q(min7), .reset(j_k_ff_1_qn));  // open: Qn, preset
endmodule

module ButtonStateHolder (
);

  wire button_1_out, clock_1_out, d_ff_1_q;

  Button button_1 (.out(button_1_out));
  Clock clock_1 (.out(clock_1_out));
  D_Flip_Flop d_ff_1 (.D(button_1_out), .clk(clock_1_out), .Q(d_ff_1_q), .preset(button_1_out));  // open: Qn, reset
  D_Flip_Flop d_ff_2 (.D(d_ff_1_q), .clk(clock_1_out));  // open: Q, Qn, preset, reset
endmodule
