// Logisim project fulladder.circ as structural Verilog: 1 circuit, main circuit main
module main (
  input  in_1,
  input  in_2,
  input  in_3
);

  wire and_1_out, and_2_out, or_1_out, xor_1_out, xor_2_out;

  xor xor_1 (xor_1_out, in_2, in_3);
  and and_1 (and_1_out, in_3, in_2);
  and and_2 (and_2_out, in_1, xor_1_out);
  xor xor_2 (xor_2_out, in_1, xor_1_out);
  or or_1 (or_1_out, and_2_out, and_1_out);
  LED led_1 (.in(xor_2_out));
  LED led_2 (.in(or_1_out));
endmodule
