// Logisim project 4bitadder.circ as structural Verilog: 3 circuits, main circuit main
module main (
  input  in00,
  input  in10,
  input  in01,
  input  in11,
  input  in02,
  input  in12,
  input  in03,
  input  in13
);

  wire fulladder_1_out0, fulladder_1_out1, fulladder_2_out0, fulladder_2_out1, fulladder_3_out0,
       fulladder_3_out1, halfadder_1_carry, halfadder_1_out0;

  halfadder halfadder_1 (.IN0(in00), .IN1(in10), .OUT0(halfadder_1_out0), .CARRY(halfadder_1_carry));
  LED led_1 (.in(halfadder_1_out0));
  fulladder fulladder_1 (
    .CARRYIN(halfadder_1_carry), .IN0(in01), .IN1(in11), .OUT0(fulladder_1_out0), .OUT1(fulladder_1_out1));
  LED led_2 (.in(fulladder_1_out0));
  LED led_3 (.in(fulladder_2_out0));
  fulladder fulladder_2 (
    .CARRYIN(fulladder_1_out1), .IN0(in02), .IN1(in12), .OUT0(fulladder_2_out0), .OUT1(fulladder_2_out1));
  fulladder fulladder_3 (
    .CARRYIN(fulladder_2_out1), .IN0(in03), .IN1(in13), .OUT0(fulladder_3_out0), .OUT1(fulladder_3_out1));
  LED led_4 (.in(fulladder_3_out0));
  LED led_5 (.in(fulladder_3_out1));

  // Notes on the sheet:
  //   out0
  //   out1
  //   out2
  //   out3
  //   overflow
  //   least significant bit (2^0)
  //   most significant bit (2^3)
endmodule

module halfadder (
  input  IN0,
  input  IN1,
  output OUT0,
  output CARRY
);

  xor xor_1 (OUT0, IN0, IN1);
  and and_1 (CARRY, IN0, IN1);
endmodule

module fulladder (
  input  CARRYIN,
  input  IN0,
  input  IN1,
  output OUT0,
  output OUT1
);

  wire halfadder_1_carry, halfadder_1_out0, halfadder_2_carry;

  halfadder halfadder_1 (.IN0(IN0), .IN1(IN1), .OUT0(halfadder_1_out0), .CARRY(halfadder_1_carry));
  halfadder halfadder_2 (.IN0(CARRYIN), .IN1(halfadder_1_out0), .OUT0(OUT0), .CARRY(halfadder_2_carry));
  or or_1 (OUT1, halfadder_2_carry, halfadder_1_carry);
endmodule
