// Logisim project dflipflop.circ as structural Verilog: 1 circuit, main circuit main
module main (
  input  SET
);

  wire and_1_out, and_2_out, CLK_out, nor_1_out, nor_2_out, not_1_out;

  Clock CLK (.out(CLK_out));
  not not_1 (not_1_out, SET);
  and and_1 (and_1_out, not_1_out, CLK_out);
  and and_2 (and_2_out, CLK_out, SET);
  nor nor_1 (nor_1_out, and_1_out, nor_2_out);
  LED Qa (.in(nor_1_out));
  nor nor_2 (nor_2_out, nor_1_out, and_2_out);
  LED Qb (.in(nor_2_out));
endmodule
