// Logisim project jkflipflop.circ as structural Verilog: 1 circuit, main circuit main
module main (
  input  J,
  input  K
);

  wire CLK_out, nand_1_out, nand_2_out, nand_3_out, nand_4_out;

  Clock CLK (.out(CLK_out));
  nand nand_1 (nand_1_out, nand_4_out, J, CLK_out);
  nand nand_2 (nand_2_out, CLK_out, K, nand_3_out);
  nand nand_3 (nand_3_out, nand_1_out, nand_4_out);
  nand nand_4 (nand_4_out, nand_3_out, nand_2_out);
  LED Qa (.in(nand_3_out));
  LED Qb (.in(nand_4_out));
endmodule
