// Logisim project bigendian3bitcommonclockcounter.circ as structural Verilog: 1 circuit, main circuit main
module main (
  input  in_1
);

  wire and_1_out, clock_1_out, j_k_ff_1_q, j_k_ff_2_q, j_k_ff_3_q;

  J_K_Flip_Flop j_k_ff_1 (.J(and_1_out), .K(and_1_out), .clk(clock_1_out), .Q(j_k_ff_1_q));  // open: Qn, preset, reset
  LED out2 (.in(j_k_ff_1_q));
  and and_1 (and_1_out, j_k_ff_3_q, j_k_ff_2_q);
  LED out1 (.in(j_k_ff_2_q));
  J_K_Flip_Flop j_k_ff_2 (
    .J(j_k_ff_3_q), .K(j_k_ff_3_q), .clk(clock_1_out), .Q(j_k_ff_2_q));  // open: Qn, preset, reset
  LED out0 (.in(j_k_ff_3_q));
  J_K_Flip_Flop j_k_ff_3 (.J(in_1), .K(in_1), .clk(clock_1_out), .Q(j_k_ff_3_q));  // open: Qn, preset, reset
  Clock clock_1 (.out(clock_1_out));
endmodule
