// Logisim project bigendian3bitcommonclockcountermod6withregister.circ as structural Verilog: 1 circuit, main circuit main
module main (
  input  in_1
);

  wire and_1_out, and_2_out, clock_1_out, d_ff_1_q, d_ff_2_q, d_ff_3_q, j_k_ff_1_q, j_k_ff_2_q, j_k_ff_3_q;

  and and_1 (and_1_out, j_k_ff_2_q, j_k_ff_1_q);
  D_Flip_Flop d_ff_1 (.D(j_k_ff_1_q), .clk(clock_1_out), .Q(d_ff_1_q));  // open: Qn, preset, reset
  J_K_Flip_Flop j_k_ff_1 (
    .J(and_2_out), .K(and_2_out), .clk(clock_1_out), .Q(j_k_ff_1_q), .reset(and_1_out));  // open: Qn, preset
  and and_2 (and_2_out, j_k_ff_3_q, j_k_ff_2_q);
  LED out2 (.in(d_ff_1_q));
  J_K_Flip_Flop j_k_ff_2 (
    .J(j_k_ff_3_q), .K(j_k_ff_3_q), .clk(clock_1_out), .Q(j_k_ff_2_q), .reset(and_1_out));  // open: Qn, preset
  LED out1 (.in(d_ff_2_q));
  D_Flip_Flop d_ff_2 (.D(j_k_ff_2_q), .clk(clock_1_out), .Q(d_ff_2_q));  // open: Qn, preset, reset
  J_K_Flip_Flop j_k_ff_3 (
    .J(in_1), .K(in_1), .clk(clock_1_out), .Q(j_k_ff_3_q), .reset(and_1_out));  // open: Qn, preset
  LED out0 (.in(d_ff_3_q));
  D_Flip_Flop d_ff_3 (.D(j_k_ff_3_q), .clk(clock_1_out), .Q(d_ff_3_q));  // open: Qn, preset, reset
  Clock clock_1 (.out(clock_1_out));
endmodule
