// Logisim project bigendian3bitcommonclockcountermod6withregisterhexdisplay.circ as structural Verilog: 1 circuit, main circuit main
module main (
  input  in_1
);

  wire and_1_out, and_2_out, clock_1_out, j_k_ff_1_q, j_k_ff_2_q, j_k_ff_3_q;
  wire [2:0] d_ff_3_q;

  and and_1 (and_1_out, j_k_ff_2_q, j_k_ff_1_q);
  Hex_Digit_Display hex_digit_display_1 (.value({1'b0, d_ff_3_q}));  // open: dp
  D_Flip_Flop d_ff_1 (.D(j_k_ff_1_q), .clk(clock_1_out), .Q(d_ff_3_q[2]));  // open: Qn, preset, reset
  J_K_Flip_Flop j_k_ff_1 (
    .J(and_2_out), .K(and_2_out), .clk(clock_1_out), .Q(j_k_ff_1_q), .reset(and_1_out));  // open: Qn, preset
  and and_2 (and_2_out, j_k_ff_3_q, j_k_ff_2_q);
  J_K_Flip_Flop j_k_ff_2 (
    .J(j_k_ff_3_q), .K(j_k_ff_3_q), .clk(clock_1_out), .Q(j_k_ff_2_q), .reset(and_1_out));  // open: Qn, preset
  D_Flip_Flop d_ff_2 (.D(j_k_ff_2_q), .clk(clock_1_out), .Q(d_ff_3_q[1]));  // open: Qn, preset, reset
  J_K_Flip_Flop j_k_ff_3 (
    .J(in_1), .K(in_1), .clk(clock_1_out), .Q(j_k_ff_3_q), .reset(and_1_out));  // open: Qn, preset
  D_Flip_Flop d_ff_3 (.D(j_k_ff_3_q), .clk(clock_1_out), .Q(d_ff_3_q[0]));  // open: Qn, preset, reset
  Clock clock_1 (.out(clock_1_out));
endmodule
