// Logisim project bigendian3bitripplecounter.circ as structural Verilog: 1 circuit, main circuit main
module main (
  input  in_1
);

  wire clock_1_out, j_k_ff_1_q, j_k_ff_2_q, j_k_ff_3_q;

  J_K_Flip_Flop #(.trigger("falling")) j_k_ff_1 (
    .J(in_1), .K(in_1), .clk(j_k_ff_2_q), .Q(j_k_ff_1_q));  // open: Qn, preset, reset
  J_K_Flip_Flop #(.trigger("falling")) j_k_ff_2 (
    .J(in_1), .K(in_1), .clk(j_k_ff_3_q), .Q(j_k_ff_2_q));  // open: Qn, preset, reset
  LED out2 (.in(j_k_ff_1_q));
  J_K_Flip_Flop #(.trigger("falling")) j_k_ff_3 (
    .J(in_1), .K(in_1), .clk(clock_1_out), .Q(j_k_ff_3_q));  // open: Qn, preset, reset
  LED out1 (.in(j_k_ff_2_q));
  LED out0 (.in(j_k_ff_3_q));
  Clock clock_1 (.out(clock_1_out));
endmodule
