// Logisim project bigendian4bitregister.circ as structural Verilog: 1 circuit, main circuit main
module main (
  input  in3,
  input  in2,
  input  in1,
  input  in0
);

  wire clock_1_out, d_ff_1_q, d_ff_2_q, d_ff_3_q, d_ff_4_q;

  Clock clock_1 (.out(clock_1_out));
  D_Flip_Flop d_ff_1 (.D(in3), .clk(clock_1_out), .Q(d_ff_1_q));  // open: Qn, preset, reset
  LED out3 (.in(d_ff_1_q));
  D_Flip_Flop d_ff_2 (.D(in2), .clk(clock_1_out), .Q(d_ff_2_q));  // open: Qn, preset, reset
  LED out2 (.in(d_ff_2_q));
  D_Flip_Flop d_ff_3 (.D(in1), .clk(clock_1_out), .Q(d_ff_3_q));  // open: Qn, preset, reset
  D_Flip_Flop d_ff_4 (.D(in0), .clk(clock_1_out), .Q(d_ff_4_q));  // open: Qn, preset, reset
  LED out1 (.in(d_ff_3_q));
  LED out0 (.in(d_ff_4_q));
endmodule
