// Logisim project stackdump.circ as structural Verilog: 1 circuit, main circuit main
module main (
  input  Direction,
  input  Data,
  input  CLR,
  input  Dump
);

  wire and_1_out, and_2_out, and_3_out, and_4_out, and_5_out, and_6_out, and_7_out, and_8_out, and_9_out,
       and_10_out, and_11_out, and_12_out, and_13_out, and_14_out, and_15_out, and_16_out, clock_1_out,
       d_ff_1_q, d_ff_2_q, d_ff_3_q, d_ff_4_q, d_ff_5_q, d_ff_6_q, d_ff_7_q, d_ff_8_q, d_ff_9_q, d_ff_10_q,
       not_1_out, or_1_out, or_2_out, or_3_out, or_4_out, or_5_out;

  Clock clock_1 (.out(clock_1_out));
  not not_1 (not_1_out, Direction);
  and and_1 (and_1_out, Data, not_1_out);
  or or_1 (or_1_out, and_1_out, and_3_out);
  and and_2 (and_2_out, Dump, clock_1_out);
  and and_3 (and_3_out, Direction, d_ff_3_q);
  D_Flip_Flop d_ff_1 (.D(or_1_out), .clk(clock_1_out), .Q(d_ff_1_q), .reset(CLR));  // open: Qn, preset
  LED out0 (.in(d_ff_1_q));
  and and_4 (and_4_out, Dump, d_ff_1_q);
  D_Flip_Flop d_ff_2 (.D(and_4_out), .clk(and_2_out), .Q(d_ff_2_q));  // open: Qn, preset, reset
  and and_5 (and_5_out, Direction, d_ff_5_q);
  and and_6 (and_6_out, d_ff_1_q, not_1_out);
  or or_2 (or_2_out, and_6_out, and_5_out);
  D_Flip_Flop d_ff_3 (.D(or_2_out), .clk(clock_1_out), .Q(d_ff_3_q), .reset(CLR));  // open: Qn, preset
  and and_7 (and_7_out, Dump, d_ff_3_q);
  D_Flip_Flop d_ff_4 (.D(and_7_out), .clk(and_2_out), .Q(d_ff_4_q));  // open: Qn, preset, reset
  LED regout0 (.in(d_ff_2_q));
  and and_8 (and_8_out, Direction, d_ff_7_q);
  and and_9 (and_9_out, d_ff_3_q, not_1_out);
  or or_3 (or_3_out, and_9_out, and_8_out);
  D_Flip_Flop d_ff_5 (.D(or_3_out), .clk(clock_1_out), .Q(d_ff_5_q), .reset(CLR));  // open: Qn, preset
  LED out1 (.in(d_ff_3_q));
  and and_10 (and_10_out, Dump, d_ff_5_q);
  LED regout1 (.in(d_ff_4_q));
  and and_11 (and_11_out, d_ff_5_q, not_1_out);
  LED out2 (.in(d_ff_5_q));
  D_Flip_Flop d_ff_6 (.D(and_10_out), .clk(and_2_out), .Q(d_ff_6_q));  // open: Qn, preset, reset
  LED regout2 (.in(d_ff_6_q));
  and and_12 (and_12_out, Direction, d_ff_9_q);
  or or_4 (or_4_out, and_11_out, and_12_out);
  D_Flip_Flop d_ff_7 (.D(or_4_out), .clk(clock_1_out), .Q(d_ff_7_q), .reset(CLR));  // open: Qn, preset
  LED out3 (.in(d_ff_7_q));
  and and_13 (and_13_out, Dump, d_ff_7_q);
  D_Flip_Flop d_ff_8 (.D(and_13_out), .clk(and_2_out), .Q(d_ff_8_q));  // open: Qn, preset, reset
  and and_14 (and_14_out, Direction, 1'b0);
  and and_15 (and_15_out, d_ff_7_q, not_1_out);
  or or_5 (or_5_out, and_15_out, and_14_out);
  D_Flip_Flop d_ff_9 (.D(or_5_out), .clk(clock_1_out), .Q(d_ff_9_q), .reset(CLR));  // open: Qn, preset
  and and_16 (and_16_out, Dump, d_ff_9_q);
  D_Flip_Flop d_ff_10 (.D(and_16_out), .clk(and_2_out), .Q(d_ff_10_q));  // open: Qn, preset, reset
  LED regout3 (.in(d_ff_8_q));
  LED out4 (.in(d_ff_9_q));
  LED regout4 (.in(d_ff_10_q));
endmodule
